// Logisim project cpu.circ as structural Verilog: 1 circuit, main circuit cpu
module cpu (
  input  clk,
  input  [31:0] Instruction,
  input  [31:0] MemReadData,
  output [31:0] MemAddress,
  output [31:0] ProgramCounter,
  output [31:0] ra,
  output [31:0] sp,
  output [31:0] t0,
  output [31:0] t1,
  output [31:0] t2,
  output [31:0] s0,
  output [31:0] s1,
  output [31:0] a0,
  output [3:0] MemWriteMask,
  output [31:0] MemWriteData
);

  wire ASel, BrEq, BrLt, BrUn, BSel, MemWEn, PCSel, regfile_1_p7, regfile_1_p8, regfile_1_p10, regfile_1_p22,
       regfile_1_p24, RegWEn;
  wire [1:0] WBSel;
  wire [2:0] funct3, ImmSel;
  wire [3:0] ALUSel;
  wire [6:0] funct7;
  wire [24:0] Instruction2;
  wire [31:0] Immediate, MemRegWriteData, multiplexer_1_out, multiplexer_2_out, multiplexer_3_out,
       multiplexer_4_out, PC_4, ProgramCounter2, RegReadData1, RegReadData2, RegWriteData;

  Adder #(.width(32)) adder_1 (.a(ProgramCounter), .b(32'h4), .out(PC_4));  // open: cin, cout
  Multiplexer #(.enable("false"), .width(32)) multiplexer_1 (
    .in0(PC_4), .in1(MemAddress), .out(multiplexer_1_out), .sel(PCSel));
  Register #(.width(32)) PC (.D(multiplexer_1_out), .en(1'b1), .clk(clk), .Q(ProgramCounter));  // open: clr
  Register #(.width(32)) register_1 (.D(ProgramCounter), .clk(clk), .Q(ProgramCounter2));  // open: en, clr
  Register #(.width(32)) register_2 (
    .D(multiplexer_2_out), .clk(clk), .Q({funct7, Instruction2[24:15], funct3, Instruction2[11:0]}));  // open: en, clr
  Multiplexer #(.enable("false"), .width(32)) multiplexer_2 (
    .in0(Instruction), .in1({32{1'b0}}), .out(multiplexer_2_out), .sel(PCSel));
  // control_logic control_logic_1: pin names not known; wires that end beside it: {funct7, Instruction2[24:15], funct3, Instruction2[11:0]}, PCSel, RegWEn, ImmSel, BrEq, BrLt
  // regfile regfile_1: pin names not known; wires that end beside it: Instruction2[19:15], Instruction2[24:20], Instruction2[11:7], RegWriteData, RegWEn, clk, regfile_1_p7, regfile_1_p8, regfile_1_p8, regfile_1_p10, ra, sp, t0, t1, t2, s0, s1, a0, RegReadData1, RegReadData2, regfile_1_p10, regfile_1_p22, regfile_1_p22, regfile_1_p24, regfile_1_p24
  imm_gen imm_gen_1 (
    .Instruction({funct7, Instruction2[24:15], funct3, Instruction2[11:0]}), .ImmSel(ImmSel),
    .Immediate(Immediate));
  Multiplexer #(.enable("false"), .width(32)) multiplexer_3 (
    .in0(RegReadData1), .in1(ProgramCounter2), .out(multiplexer_3_out), .sel(ASel));
  Multiplexer #(.enable("false"), .width(32)) multiplexer_4 (
    .in0(RegReadData2), .in1(Immediate), .out(multiplexer_4_out), .sel(BSel));
  alu alu_1 (.ALUResult(MemAddress), .A(multiplexer_3_out), .B(multiplexer_4_out), .ALUSel(ALUSel));
  branch_comp branch_comp_1 (.BrData1(RegReadData1), .BrData2(RegReadData2), .BrUn(BrUn), .BrEq(BrEq), .BrLt(BrLt));
  Multiplexer #(.enable("false"), .select(2), .width(32)) multiplexer_5 (
    .in0(MemRegWriteData), .in1(MemAddress), .in2(PC_4), .out(RegWriteData), .sel(WBSel));  // open: in3
  partial_store partial_store_1 (
    .Instruction({funct7, Instruction2[24:15], funct3, Instruction2[11:0]}), .MemAddress(MemAddress),
    .DataFromReg(RegReadData2), .MemWEn(MemWEn), .MemWriteMask(MemWriteMask), .DataToMem(MemWriteData));
  partial_load partial_load_1 (
    .Instruction({funct7, Instruction2[24:15], funct3, Instruction2[11:0]}), .MemAddress(MemAddress),
    .DataFromMem(MemReadData), .DataToReg(MemRegWriteData));

  // Other names for the same wires on the sheet: ALUData[31:0] = MemAddress; Instruction1[31:0] = Instruction;
  //   opcode[6:0] = Instruction2[6:0]; WriteReg[4:0] = Instruction2[11:7];
  //   Instruction2 (some bits) = {funct7, funct3}; ReadReg1[4:0] = Instruction2[19:15];
  //   ReadReg2[4:0] = Instruction2[24:20]; ProgramCounter1[31:0] = ProgramCounter

  // Notes on the sheet:
  //   To IMEM
  //   IMEM (do **NOT** move this)
  //   From IMEM
  //   Inputs/Outputs for testing. Do **NOT** move these.
  //   It is OK to move the PC, RegFile, ALU, MEM, Branch Comp, Imm Gen, Partial Load, Partial Store and Control Logic to wherever is most convenient for you when constructing your CPU, and to delete this text
  //   To DMEM
  //   DMEM (do **NOT** move this)
  //   From DMEM
endmodule
