// Logisim project partial-load.circ as structural Verilog: 1 circuit, main circuit partial_load
module partial_load (
  input  [31:0] Instruction,
  input  [31:0] MemAddress,
  input  [31:0] DataFromMem,
  output [31:0] DataToReg
);

  wire [7:7] multiplexer_1_out;
  wire [15:15] multiplexer_2_out;
  wire [31:0] lbData, lhData;

  Multiplexer #(.enable("false"), .select(2), .width(8)) multiplexer_1 (
    .in0(DataFromMem[7:0]), .in1(DataFromMem[15:8]), .in2(DataFromMem[23:16]), .in3(DataFromMem[31:24]),
    .out({multiplexer_1_out[7], lbData[6:0]}), .sel(MemAddress[1:0]));
  Multiplexer #(.enable("false"), .select(2), .width(16)) multiplexer_2 (
    .in0(DataFromMem[15:0]), .in1(DataFromMem[23:8]), .in2(DataFromMem[31:16]),
    .out({multiplexer_2_out[15], lhData[14:0]}), .sel(MemAddress[1:0]));  // open: in3
  Multiplexer #(.enable("false"), .width(25)) multiplexer_3 (
    .in0({25{1'b0}}), .in1({25{1'b1}}), .out(lbData[31:7]), .sel(multiplexer_1_out[7]));
  Multiplexer #(.enable("false"), .width(17)) multiplexer_4 (
    .in0({17{1'b0}}), .in1({17{1'b1}}), .out(lhData[31:15]), .sel(multiplexer_2_out[15]));
  Multiplexer #(.enable("false"), .select(3), .width(32)) multiplexer_5 (
    .in0(lbData), .in1(lhData), .in2(DataFromMem), .out(DataToReg), .sel(Instruction[14:12]));  // open: in3, in4, in5, in6, in7

  // Other names for the same wires on the sheet: opcode[6:0] = Instruction[6:0]; WriteReg[4:0] = Instruction[11:7];
  //   funct3[2:0] = Instruction[14:12]; ReadReg1[4:0] = Instruction[19:15]; ReadReg2[4:0] = Instruction[24:20];
  //   funct7[6:0] = Instruction[31:25]; lwData[31:0] = DataFromMem

  // Notes on the sheet:
  //   INPUTS to your circuit
  //   DON'T CHANGE THE LOCATIONS OF THE INPUTS AND OUTPUTS!
  //   OUTPUT from your circuit
endmodule
