// Logisim project partial-store.circ as structural Verilog: 1 circuit, main circuit partial_store
module partial_store (
  input  [31:0] Instruction,
  input  [31:0] MemAddress,
  input  [31:0] DataFromReg,
  input  MemWEn,
  output [3:0] MemWriteMask,
  output [31:0] DataToMem
);

  wire comparator_1_eq;
  wire [3:0] Mask, sbMemWriteMask, shMemWriteMask, swMemWriteMask;
  wire [31:0] Data, sbData, shData, swData;

  Multiplexer #(.enable("false"), .select(2), .width(4)) multiplexer_1 (
    .in0(4'b0001), .in1(4'b0010), .in2(4'b0100), .in3(4'b1000), .out(sbMemWriteMask), .sel(MemAddress[1:0]));
  Multiplexer #(.enable("false"), .width(32)) multiplexer_2 (
    .in0({32{1'b0}}), .in1(Data), .out(DataToMem), .sel(comparator_1_eq));
  Comparator #(.width(7)) comparator_1 (.a(Instruction[6:0]), .b(7'b0100011), .eq(comparator_1_eq));  // open: gt, lt
  Multiplexer #(.enable("false"), .select(2), .width(4)) multiplexer_3 (
    .in0(4'b1111), .out(swMemWriteMask), .sel(MemAddress[1:0]));  // open: in1, in2, in3
  Multiplexer #(.enable("false"), .select(2), .width(32)) multiplexer_4 (
    .in0({{24{1'b0}}, DataFromReg[7:0]}), .in1({{16{1'b0}}, DataFromReg[7:0], {8{1'b0}}}),
    .in2({{8{1'b0}}, DataFromReg[7:0], {16{1'b0}}}), .in3({DataFromReg[7:0], {24{1'b0}}}), .out(sbData),
    .sel(MemAddress[1:0]));
  Multiplexer #(.enable("false"), .select(2), .width(32)) multiplexer_5 (
    .in0(DataFromReg), .out(swData), .sel(MemAddress[1:0]));  // open: in1, in2, in3
  Multiplexer #(.enable("false"), .width(4)) multiplexer_6 (
    .in0(4'b0000), .in1(Mask), .out(MemWriteMask), .sel(comparator_1_eq));
  Multiplexer #(.enable("false"), .select(3), .width(32)) multiplexer_7 (
    .in0(sbData), .in1(shData), .in2(swData), .out(Data), .sel(Instruction[14:12]));  // open: in3, in4, in5, in6, in7
  Multiplexer #(.enable("false"), .select(2), .width(4)) multiplexer_8 (
    .in0(4'b0011), .in2(4'b1100), .out(shMemWriteMask), .sel(MemAddress[1:0]));  // open: in1, in3
  Multiplexer #(.enable("false"), .select(2), .width(32)) multiplexer_9 (
    .in0({{16{1'b0}}, DataFromReg[15:0]}), .in2({DataFromReg[15:0], {16{1'b0}}}), .out(shData),
    .sel(MemAddress[1:0]));  // open: in1, in3
  Multiplexer #(.enable("false"), .select(3), .width(4)) multiplexer_10 (
    .in0(sbMemWriteMask), .in1(shMemWriteMask), .in2(swMemWriteMask), .in3(4'b0000), .in4(4'b0000),
    .in5(4'b0000), .in6(4'b0000), .in7(4'b0000), .out(Mask), .sel(Instruction[14:12]));

  // Other names for the same wires on the sheet: opcode[6:0] = Instruction[6:0]; WriteReg[4:0] = Instruction[11:7];
  //   funct3[2:0] = Instruction[14:12]; ReadReg1[4:0] = Instruction[19:15]; ReadReg2[4:0] = Instruction[24:20];
  //   funct7[6:0] = Instruction[31:25]

  // Notes on the sheet:
  //   INPUTS to your circuit
  //   DON'T CHANGE THE LOCATIONS OF THE INPUTS AND OUTPUTS!
  //   OUTPUT from your circuit
endmodule
